// Logisim project 7 SegmentDisplay.circ as structural Verilog: 2 circuits, main circuit main
module main (
  input  [3:0] in_1
);

  wire display_7_segmentos_1_a, display_7_segmentos_1_b, display_7_segmentos_1_c, display_7_segmentos_1_d,
       display_7_segmentos_1_e, display_7_segmentos_1_f, display_7_segmentos_1_g;

  Display_7_segmentos display_7_segmentos_1 (
    .w(in_1[3]), .x(in_1[2]), .y(in_1[1]), .z(in_1[0]), .a(display_7_segmentos_1_a),
    .b(display_7_segmentos_1_b), .c(display_7_segmentos_1_c), .d(display_7_segmentos_1_d),
    .e(display_7_segmentos_1_e), .f(display_7_segmentos_1_f), .g(display_7_segmentos_1_g));
  _7_Segment_Display u_7_segment_display_1 (
    .g(display_7_segmentos_1_g), .f(display_7_segmentos_1_f), .a(display_7_segmentos_1_a),
    .b(display_7_segmentos_1_b), .e(display_7_segmentos_1_e), .d(display_7_segmentos_1_d),
    .c(display_7_segmentos_1_c));  // open: dp
endmodule

module Display_7_segmentos (
  input  w,
  input  x,
  input  y,
  input  z,
  output a,
  output b,
  output c,
  output d,
  output e,
  output f,
  output g
);

  wire and_1_out, and_2_out, and_3_out, and_4_out, and_5_out, and_6_out, and_7_out, and_8_out, and_9_out,
       and_10_out, and_11_out, and_12_out, and_13_out, and_14_out, and_15_out, and_16_out, not_1_out,
       not_2_out, not_3_out, not_4_out, not_5_out, not_6_out, not_7_out, not_8_out, not_9_out, not_10_out,
       not_11_out, not_12_out, not_13_out, not_14_out, not_15_out, not_16_out, not_17_out, not_18_out,
       not_19_out, not_20_out, not_21_out;

  not not_1 (not_1_out, x);
  and and_1 (and_1_out, not_1_out, not_2_out);
  not not_2 (not_2_out, z);
  and and_2 (and_2_out, x, z);
  not not_3 (not_3_out, x);
  not not_4 (not_4_out, y);
  and and_3 (and_3_out, not_4_out, not_5_out);
  not not_5 (not_5_out, z);
  and and_4 (and_4_out, y, z);
  not not_6 (not_6_out, y);
  or or_1 (c, not_6_out, z, x);
  not not_7 (not_7_out, x);
  and and_5 (and_5_out, not_7_out, not_8_out);
  not not_8 (not_8_out, z);
  not not_9 (not_9_out, x);
  and and_6 (and_6_out, not_9_out, y);
  and and_7 (and_7_out, y, not_10_out);
  not not_10 (not_10_out, z);
  not not_11 (not_11_out, y);
  and and_8 (and_8_out, x, not_11_out, z);
  not not_12 (not_12_out, x);
  and and_9 (and_9_out, not_12_out, not_13_out);
  not not_13 (not_13_out, z);
  and and_10 (and_10_out, y, not_14_out);
  not not_14 (not_14_out, z);
  not not_15 (not_15_out, y);
  and and_11 (and_11_out, not_15_out, not_16_out);
  not not_16 (not_16_out, z);
  and and_12 (and_12_out, x, not_17_out);
  not not_17 (not_17_out, y);
  and and_13 (and_13_out, x, not_18_out);
  not not_18 (not_18_out, z);
  not not_19 (not_19_out, x);
  and and_14 (and_14_out, not_19_out, y);
  and and_15 (and_15_out, x, not_20_out);
  not not_20 (not_20_out, y);
  and and_16 (and_16_out, x, not_21_out);
  not not_21 (not_21_out, z);
  or or_2 (a, and_1_out, y, and_2_out, w);
  or or_3 (b, not_3_out, and_3_out, and_4_out);
  or or_4 (d, and_5_out, and_6_out, and_7_out, and_8_out, w);
  or or_5 (e, and_9_out, and_10_out);
  or or_6 (f, and_11_out, and_12_out, and_13_out, w);
  or or_7 (g, and_14_out, and_15_out, and_16_out, w);
endmodule
